// Logisim project 1931461642_EmonSarker v2.circ as structural Verilog: 4 circuits, main circuit Datapath
module ALU_2 (
  input  [15:0] A,
  input  [15:0] B,
  input  A_inv,
  input  B_inv,
  input  Cin,
  input  [1:0] ALU_OP,
  output Cout,
  output [15:0] Output,
  output Zero
);

  wire comparator_1_lt;
  wire [3:0] bit_extender_1_out;
  wire [15:0] adder_1_out, and_1_out, bit_extender_2_out, multiplexer_1_out, multiplexer_2_out, not_1_out,
       not_2_out, shifter_1_out;

  assign not_1_out = ~A;  // NOT_Gate not_1, 16 bits wide
  Multiplexer #(.width(16)) multiplexer_1 (.in0(A), .in1(not_1_out), .out(multiplexer_1_out), .sel(A_inv));  // open: en
  assign not_2_out = ~B;  // NOT_Gate not_2, 16 bits wide
  Multiplexer #(.width(16)) multiplexer_2 (.in0(B), .in1(not_2_out), .out(multiplexer_2_out), .sel(B_inv));  // open: en
  Bit_Extender #(.in_width(16), .out_width(4)) bit_extender_1 (.in(multiplexer_2_out), .out(bit_extender_1_out));
  assign and_1_out = multiplexer_1_out & multiplexer_2_out;  // AND_Gate and_1, 16 bits wide
  Adder #(.width(16)) adder_1 (.a(multiplexer_1_out), .b(multiplexer_2_out), .out(adder_1_out), .cin(Cin), .cout(Cout));
  Comparator #(.width(16)) comparator_1 (
    .a(multiplexer_1_out), .b(multiplexer_2_out), .lt(comparator_1_lt));  // open: gt, eq
  Shifter #(.width(16)) shifter_1 (.in(multiplexer_1_out), .\dist (bit_extender_1_out), .out(shifter_1_out));
  assign bit_extender_2_out = {{15{1'b0}}, comparator_1_lt};  // Bit_Extender bit_extender_2
  Multiplexer #(.select(2), .width(16)) multiplexer_3 (
    .in0(adder_1_out), .in1(shifter_1_out), .in2(and_1_out), .in3(bit_extender_2_out), .out(Output),
    .sel(ALU_OP));  // open: en
  nor nor_1 (Zero, Output[0], Output[1], Output[2], Output[3], Output[4], Output[5], Output[6], Output[7], Output[8], Output[9], Output[10], Output[11], Output[12], Output[13], Output[14], Output[15]);

  // Notes on the sheet:
  //   Instruction
  //   nop
  //   sub/add/addi
  //   sw/lw/beq
  //   sll
  //   AND
  //   sit
  //   OP
  //   000
  //   001
  //   010
  //   011
  //   100
endmodule

module Register (
  input  [15:0] Write_Data,
  input  [3:0] Read_Reg_1,
  input  [3:0] Data_Input,
  input  [3:0] Read_Reg_2,
  input  Enabler,
  input  Clock,
  input  Clear,
  output [15:0] Read_Data_1,
  output [15:0] Read_Data_2
);

  wire and_1_out, and_2_out, and_3_out, and_4_out, and_5_out, and_6_out, and_7_out, and_8_out, and_9_out,
       and_10_out, and_11_out, and_12_out, and_13_out, and_14_out, and_15_out, decoder_1_out1,
       decoder_1_out2, decoder_1_out3, decoder_1_out4, decoder_1_out5, decoder_1_out6, decoder_1_out7,
       decoder_1_out8, decoder_1_out9, decoder_1_out10, decoder_1_out11, decoder_1_out12, decoder_1_out13,
       decoder_1_out14, decoder_1_out15;
  wire [15:0] R0_q, R1_q, R2_q, R3_q, R4_q, R5_q, R6_q, R7_q, R8_q, R9_q, R10_q, R11_q, R12_q, R13_q, R14_q,
       R15_q;

  Decoder #(.select(4)) decoder_1 (
    .out1(decoder_1_out1), .out2(decoder_1_out2), .out3(decoder_1_out3), .out4(decoder_1_out4),
    .out5(decoder_1_out5), .out6(decoder_1_out6), .out7(decoder_1_out7), .out8(decoder_1_out8),
    .out9(decoder_1_out9), .out10(decoder_1_out10), .out11(decoder_1_out11), .out12(decoder_1_out12),
    .out13(decoder_1_out13), .out14(decoder_1_out14), .out15(decoder_1_out15), .sel(Data_Input));  // open: out0, en
  and and_1 (and_1_out, decoder_1_out1, Enabler);
  and and_2 (and_2_out, decoder_1_out2, Enabler);
  and and_3 (and_3_out, decoder_1_out3, Enabler);
  and and_4 (and_4_out, decoder_1_out4, Enabler);
  and and_5 (and_5_out, decoder_1_out5, Enabler);
  and and_6 (and_6_out, decoder_1_out6, Enabler);
  and and_7 (and_7_out, decoder_1_out7, Enabler);
  and and_8 (and_8_out, decoder_1_out8, Enabler);
  and and_9 (and_9_out, decoder_1_out9, Enabler);
  and and_10 (and_10_out, decoder_1_out10, Enabler);
  and and_11 (and_11_out, decoder_1_out11, Enabler);
  and and_12 (and_12_out, decoder_1_out12, Enabler);
  and and_13 (and_13_out, decoder_1_out13, Enabler);
  and and_14 (and_14_out, decoder_1_out14, Enabler);
  and and_15 (and_15_out, decoder_1_out15, Enabler);
  Register_part #(.width(16)) R0 (.D(Write_Data), .en(1'b0), .Q(R0_q), .clk(Clock), .clr(Clear));
  Register_part #(.width(16)) R1 (.D(Write_Data), .en(and_1_out), .Q(R1_q), .clk(Clock), .clr(Clear));
  Register_part #(.width(16)) R2 (.D(Write_Data), .en(and_2_out), .Q(R2_q), .clk(Clock), .clr(Clear));
  Register_part #(.width(16)) R3 (.D(Write_Data), .en(and_3_out), .Q(R3_q), .clk(Clock), .clr(Clear));
  Register_part #(.width(16)) R4 (.D(Write_Data), .en(and_4_out), .Q(R4_q), .clk(Clock), .clr(Clear));
  Register_part #(.width(16)) R5 (.D(Write_Data), .en(and_5_out), .Q(R5_q), .clk(Clock), .clr(Clear));
  Register_part #(.width(16)) R6 (.D(Write_Data), .en(and_6_out), .Q(R6_q), .clk(Clock), .clr(Clear));
  Register_part #(.width(16)) R7 (.D(Write_Data), .en(and_7_out), .Q(R7_q), .clk(Clock), .clr(Clear));
  Register_part #(.width(16)) R8 (.D(Write_Data), .en(and_8_out), .Q(R8_q), .clk(Clock), .clr(Clear));
  Register_part #(.width(16)) R9 (.D(Write_Data), .en(and_9_out), .Q(R9_q), .clk(Clock), .clr(Clear));
  Register_part #(.width(16)) R10 (.D(Write_Data), .en(and_10_out), .Q(R10_q), .clk(Clock), .clr(Clear));
  Register_part #(.width(16)) R11 (.D(Write_Data), .en(and_11_out), .Q(R11_q), .clk(Clock), .clr(Clear));
  Register_part #(.width(16)) R12 (.D(Write_Data), .en(and_12_out), .Q(R12_q), .clk(Clock), .clr(Clear));
  Register_part #(.width(16)) R13 (.D(Write_Data), .en(and_13_out), .Q(R13_q), .clk(Clock), .clr(Clear));
  Register_part #(.width(16)) R14 (.D(Write_Data), .en(and_14_out), .Q(R14_q), .clk(Clock), .clr(Clear));
  Register_part #(.width(16)) R15 (.D(Write_Data), .en(and_15_out), .Q(R15_q), .clk(Clock), .clr(Clear));
  Multiplexer #(.select(4), .width(16)) multiplexer_1 (
    .in0(R0_q), .in1(R1_q), .in2(R2_q), .in3(R3_q), .in4(R4_q), .in5(R5_q), .in6(R6_q), .in7(R7_q),
    .in8(R8_q), .in9(R9_q), .in10(R10_q), .in11(R11_q), .in12(R12_q), .in13(R13_q), .in14(R14_q),
    .in15(R15_q), .out(Read_Data_1), .sel(Read_Reg_1));  // open: en
  Multiplexer #(.select(4), .width(16)) multiplexer_2 (
    .in0(R0_q), .in1(R1_q), .in2(R2_q), .in3(R3_q), .in4(R4_q), .in5(R5_q), .in6(R6_q), .in7(R7_q),
    .in8(R8_q), .in9(R9_q), .in10(R10_q), .in11(R11_q), .in12(R12_q), .in13(R13_q), .in14(R14_q),
    .in15(R15_q), .out(Read_Data_2), .sel(Read_Reg_2));  // open: en
endmodule

module Datapath (
  input  in_1,
  input  in_2,
  input  in_3,
  input  Clock,
  output [3:0] OP,
  output [15:0] A,
  output [3:0] RS,
  output [15:0] out_8,
  output [3:0] RT,
  output [15:0] B,
  output [3:0] RD,
  output out_12,
  output out_13,
  output [15:0] out_14,
  output [15:0] out_15
);

  wire and_1_out, beq, control_unit_1_bin, control_unit_1_cin, control_unit_1_ram, control_unit_1_ram_read,
       control_unit_1_ram_to_reg, control_unit_1_ram_write, control_unit_1_rd_im, control_unit_1_rt_rd,
       control_unit_1_write_enable, jmp;
  wire [1:0] control_unit_1_alu_op;
  wire [3:0] multiplexer_1_out;
  wire [15:0] adder_1_out, bit_extender_1_out, bit_extender_2_out, multiplexer_3_out, multiplexer_4_out,
       multiplexer_5_out, ram_1_data, register_1_q;

  Register_part #(.width(16)) register_1 (
    .D(multiplexer_4_out), .Q(register_1_q), .clk(Clock), .clr(in_1));  // open: en
  Adder #(.width(16)) adder_1 (.a(16'h1), .b(register_1_q), .out(adder_1_out), .cin(1'b0));  // open: cout
  assign bit_extender_1_out = {{4{1'b0}}, {RS, RT, RD}};  // Bit_Extender bit_extender_1
  ROM #(.addrWidth(16), .dataWidth(16)) rom_1 (.addr(register_1_q), .data({OP, RS, RT, RD}));  // open: sel
  Control_Unit control_unit_1 (
    .OP_code(OP), .ALU_OP(control_unit_1_alu_op), .Cin(control_unit_1_cin), .Bin(control_unit_1_bin),
    .Write_Enable(control_unit_1_write_enable), .RT_RD(control_unit_1_rt_rd), .RD_IM(control_unit_1_rd_im),
    .RAM(control_unit_1_ram), .beq(beq), .jmp(jmp), .RAM_Read(control_unit_1_ram_read),
    .RAM_Write(control_unit_1_ram_write), .RAM_to_Reg(control_unit_1_ram_to_reg));
  Multiplexer #(.width(4)) multiplexer_1 (
    .in0(RT), .in1(RD), .out(multiplexer_1_out), .sel(control_unit_1_rt_rd));  // open: en
  Register register_2 (
    .Write_Data(multiplexer_5_out), .Read_Reg_1(RS), .Data_Input(multiplexer_1_out), .Read_Reg_2(RT),
    .Enabler(control_unit_1_write_enable), .Read_Data_1(A), .Read_Data_2(B), .Clock(Clock), .Clear(in_2));
  assign bit_extender_2_out = {{12{1'b0}}, RD};  // Bit_Extender bit_extender_2
  Multiplexer #(.width(16)) multiplexer_2 (
    .in0(B), .in1(bit_extender_2_out), .out(out_15), .sel(control_unit_1_rd_im));  // open: en
  Multiplexer #(.width(16)) multiplexer_3 (
    .in0(adder_1_out), .in1(bit_extender_2_out), .out(multiplexer_3_out), .sel(and_1_out));  // open: en
  and and_1 (and_1_out, beq, out_12);
  Multiplexer #(.width(16)) multiplexer_4 (
    .in0(multiplexer_3_out), .in1(bit_extender_1_out), .out(multiplexer_4_out), .sel(jmp));  // open: en
  ALU_2 alu_2_1 (
    .A_inv(in_3), .B_inv(control_unit_1_bin), .Output(out_8), .Zero(out_12), .A(A), .B(out_15),
    .Cin(control_unit_1_cin), .Cout(out_13), .ALU_OP(control_unit_1_alu_op));
  RAM #(.addrWidth(16), .dataWidth(16), .bus("separate")) ram_1 (
    .addr(out_8), .din(A), .data(ram_1_data), .str(control_unit_1_ram_write), .sel(control_unit_1_ram),
    .clk(Clock), .ld(control_unit_1_ram_read));  // open: clr
  Multiplexer #(.width(16)) multiplexer_5 (
    .in0(out_8), .in1(ram_1_data), .out(multiplexer_5_out), .sel(control_unit_1_ram_to_reg));  // open: en

  assign out_14 = A;

  // Other names for the same wires on the sheet: OP_CODE[3:0] = OP

  // Notes on the sheet:
  //   contents of rom_1 (hex, n*v repeats v):
  //   5027 5127 5020 5121 5220 1111
endmodule

module Control_Unit (
  input  [3:0] OP_code,
  output [1:0] ALU_OP,
  output Cin,
  output Bin,
  output Write_Enable,
  output RT_RD,
  output RD_IM,
  output RAM,
  output RAM_Read,
  output RAM_Write,
  output RAM_to_Reg,
  output beq,
  output jmp
);

  wire decoder_1_out0, decoder_1_out2, decoder_1_out3, decoder_1_out4, decoder_1_out6, decoder_1_out8,
       decoder_1_out9;

  Decoder #(.select(4)) decoder_1 (
    .out0(decoder_1_out0), .out1(beq), .out2(decoder_1_out2), .out3(decoder_1_out3), .out4(decoder_1_out4),
    .out5(RAM_Write), .out6(decoder_1_out6), .out7(jmp), .out8(decoder_1_out8), .out9(decoder_1_out9),
    .out10(RAM_Read), .sel(OP_code));  // open: out11, out12, out13, out14, out15, en
  or or_1 (ALU_OP[0], decoder_1_out6, decoder_1_out3);
  or or_2 (ALU_OP[1], decoder_1_out4, decoder_1_out6);
  or or_3 (Cin, beq, decoder_1_out2);
  or or_4 (Bin, beq, decoder_1_out2);
  or or_5 (Write_Enable, decoder_1_out2, decoder_1_out3, decoder_1_out4, decoder_1_out6, decoder_1_out8, decoder_1_out9, RAM_Read);
  or or_6 (RT_RD, beq, decoder_1_out2, decoder_1_out4, decoder_1_out6, jmp, decoder_1_out8);
  or or_7 (RD_IM, RAM_Read, RAM_Write, decoder_1_out9, decoder_1_out3);
  or or_8 (RAM, RAM_Write, RAM_Read);
  or or_9 (RAM_to_Reg, RAM_Write, RAM_Read);
endmodule
